# Fritzing sketch facetracker (saved by Fritzing 0.9.2b)
breadboards: 1

parts:
  Part1 = RedBear-Duo
  LED1 = LED - 5mm [color="Red (633nm)" package="5 mm [THT]"]  # not connected
  J1 = Piezo Speaker
  Part2 = SRF05 Ultrasonic Rangefinder
  J2 = Basic Servo  # not connected
  R1 = Resistor [tolerance=±5% resistance=220 package=THT]  # not connected
  VCC1 = 4 x AAA Battery Mount

nets:
  N1: Part1.A0, J1.pin2
  GND: Part1.GND, J1.pin1, Part2.GND, VCC1.-
  N2: Part1.D0, Part2.Trig
  N3: Part1.D1, Part2.Echo
  N4: Part2.VCC, VCC1.+

notes:
  Pretend this is 3 batteries

custom parts:
  RedBear-Duo: Duo is a thumb-size development board made to simplify the building process of Internet of Things (IoT). This part is a modification of the Particle Photon part by Brett Walach,Fabian Althaus
